# Fritzing sketch esp32.with.dht22 (saved by Fritzing 0.9.2b)
breadboards: 1

parts:
  RHT1 = Humidity and Temperature Sensor RHT03
  R1 = Resistor [tolerance=±5% resistance=10k package=THT]
  U1 = ESP32-38PinWide [part_number=ESP32-38PinWide]

nets:
  N1: RHT1.Vcc, R1.Pin_1, U1.3.3
  N2: RHT1.Data-signal, R1.Pin_0, U1.GPIO13
  N3: RHT1.GND_2, U1.GND

custom parts:
  ESP32-38PinWide: Generic 38-Pin ESP32 with wide format (only access to one side of pins on a breadboard) based on Stephen Lilley's HiLetgo ESP-WROOM-32 ESP32 ESP-32S Development Board.
