# Fritzing sketch esp32.with.lcd1602 (saved by Fritzing 0.9.4)
breadboards: 1

parts:
  Súčiastka1 = LCD1602-I2C
  U2 = ESP32-38PinWide [part_number=ESP32-38PinWide]
  R1 = Resistor [tolerance=±5% resistance=4.7k package="1206 [SMD]"]
  R2 = Resistor [tolerance=±5% resistance=4.7k package="1206 [SMD]"]

nets:
  GND: Súčiastka1.GND, U2.GND
  N1: Súčiastka1.VCC, U2.3.3, R1.Pin_0, R2.Pin_0
  N2: Súčiastka1.SDA, U2.GPIO22, R2.Pin_1
  N3: Súčiastka1.SCL, U2.GPIO23, R1.Pin_1

custom parts:
  LCD1602-I2C: A standard character display, usually with 2x16 characters. Comes in many colors with LCM1602 IIC attached.
  ESP32-38PinWide: Generic 38-Pin ESP32 with wide format (only access to one side of pins on a breadboard) based on Stephen Lilley's HiLetgo ESP-WROOM-32 ESP32 ESP-32S Development Board.
