# Fritzing sketch esp32.with.pir (saved by Fritzing 0.9.4)
breadboards: 1

parts:
  U2 = ESP32-38PinWide [part_number=ESP32-38PinWide]
  R1 = Resistor [tolerance=±5% resistance=10k package="1206 [SMD]"]
  R3 = PHOTOCELL [package=photocell]

nets:
  N1: U2.3.3, R1.Pin_1
  N2: U2.GPIO33, R1.Pin_0, R3.P$1
  N3: U2.GND, R3.P$2

custom parts:
  ESP32-38PinWide: Generic 38-Pin ESP32 with wide format (only access to one side of pins on a breadboard) based on Stephen Lilley's HiLetgo ESP-WROOM-32 ESP32 ESP-32S Development Board.
