# Fritzing sketch esp32.with.tmp36 (saved by Fritzing 0.9.3b)
breadboards: 1

parts:
  U1 = ESP32-38PinWide [part_number=ESP32-38PinWide]
  T1 = TMP36 Temperature Sensor [package="TO92 [THT]"]

nets:
  N1: U1.3.3, T1.GND
  N2: U1.GPIO33, T1.Vout
  N3: U1.GND, T1.+Vs

custom parts:
  ESP32-38PinWide: Generic 38-Pin ESP32 with wide format (only access to one side of pins on a breadboard) based on Stephen Lilley's HiLetgo ESP-WROOM-32 ESP32 ESP-32S Development Board.
